// Logisim project project_2_14_6.circ as structural Verilog
module HalfAdder (
  input  A,
  input  B,
  output Sum,
  output Count
);

  wire and_1_out, and_2_out, not_1_out, not_2_out;

  not not_1 (not_1_out, B);
  not not_2 (not_2_out, A);
  and and_1 (and_1_out, A, not_1_out);
  and and_2 (and_2_out, B, not_2_out);
  and and_3 (Count, A, B);
  or or_1 (Sum, and_1_out, and_2_out);
endmodule

module FullAdder (
  input  A,
  input  B,
  input  Cin,
  output Sum,
  output Count
);

  wire halfadder_1_count, halfadder_1_sum, halfadder_2_count;

  HalfAdder halfadder_1 (.A(A), .B(B), .Sum(halfadder_1_sum), .Count(halfadder_1_count));
  HalfAdder halfadder_2 (.A(Cin), .B(halfadder_1_sum), .Sum(Sum), .Count(halfadder_2_count));
  or or_1 (Count, halfadder_2_count, halfadder_1_count);
endmodule

module Multiplexer1 (
  input  A,
  input  B,
  input  C,
  output out_4
);

  wire and_1_out, and_2_out, not_1_out;

  not not_1 (not_1_out, B);
  and and_1 (and_1_out, A, not_1_out);
  and and_2 (and_2_out, B, C);
  or or_1 (out_4, and_1_out, and_2_out);
endmodule

module OneBitShiftRegisterv2 (
  input  inp,
  input  en,
  input  clk,
  input  rst,
  output out_5,
  output out_6,
  output out_7,
  output out_8
);

  wire and_1_out, dlatch_1_q, not_1_out;

  not not_1 (not_1_out, clk);
  DLatch dlatch_1 (.D(en), .Clk(not_1_out), .Q(dlatch_1_q));  // open: NotQ
  and and_1 (and_1_out, dlatch_1_q, clk);
  DFlipFlop dflipflop_1 (.D(inp), .Rst(rst), .Clk(and_1_out), .Q(out_8));  // open: NotQ
  DFlipFlop dflipflop_2 (.D(out_8), .Rst(rst), .Clk(and_1_out), .Q(out_6));  // open: NotQ
  DFlipFlop dflipflop_3 (.D(out_6), .Rst(rst), .Clk(and_1_out), .Q(out_5));  // open: NotQ
  DFlipFlop dflipflop_4 (.D(out_5), .Rst(rst), .Clk(and_1_out), .Q(out_7));  // open: NotQ
endmodule

module FourBitShiftRegisterv2 (
  input  reset,
  input  load,
  input  shift,
  input  clk,
  input  d4,
  input  d3,
  input  d2,
  input  d1,
  input  sin,
  output q1,
  output q2,
  output q3,
  output q4
);

  wire and_1_out, dlatch_1_q, multiplexer1_1_out_4, multiplexer1_2_out_4, multiplexer1_3_out_4,
       multiplexer1_4_out_4, not_1_out, not_2_out, not_3_out, or_1_out;

  not not_1 (not_1_out, load);
  not not_2 (not_2_out, load);
  or or_1 (or_1_out, load, shift);
  not not_3 (not_3_out, clk);
  DLatch dlatch_1 (.D(or_1_out), .Clk(not_3_out), .Q(dlatch_1_q));  // open: NotQ
  Multiplexer1 multiplexer1_1 (.A(d4), .B(not_2_out), .C(sin), .out_4(multiplexer1_1_out_4));
  and and_1 (and_1_out, dlatch_1_q, clk);
  DFlipFlop dflipflop_1 (.D(multiplexer1_1_out_4), .Rst(reset), .Clk(and_1_out), .Q(q4));  // open: NotQ
  Multiplexer1 multiplexer1_2 (.A(d3), .B(not_1_out), .C(q4), .out_4(multiplexer1_2_out_4));
  DFlipFlop dflipflop_2 (.D(multiplexer1_2_out_4), .Rst(reset), .Clk(and_1_out), .Q(q3));  // open: NotQ
  Multiplexer1 multiplexer1_3 (.A(d2), .B(not_1_out), .C(q3), .out_4(multiplexer1_3_out_4));
  DFlipFlop dflipflop_3 (.D(multiplexer1_3_out_4), .Rst(reset), .Clk(and_1_out), .Q(q2));  // open: NotQ
  Multiplexer1 multiplexer1_4 (.A(d1), .B(not_1_out), .C(q2), .out_4(multiplexer1_4_out_4));
  DFlipFlop dflipflop_4 (.D(multiplexer1_4_out_4), .Rst(reset), .Clk(and_1_out), .Q(q1));  // open: NotQ
endmodule

module SerialAdderv2 (
  input  load,
  input  shift,
  input  clk,
  input  inp,
  input  reset,
  output out_6,
  output out_7,
  output out_8,
  output out_9,
  output out_10,
  output out_11,
  output out_12,
  output out_13
);

  wire dflipflop_1_q, fulladder_1_count, fulladder_1_sum;

  FourBitShiftRegisterv2 fourbitshiftregisterv2_1 (
    .reset(reset), .load(load), .shift(shift), .clk(clk), .sin(fulladder_1_sum), .q1(out_6), .q2(out_7),
    .q3(out_8), .q4(out_9));  // open: d4, d3, d2, d1
  FourBitShiftRegisterv2 fourbitshiftregisterv2_2 (
    .reset(reset), .load(load), .shift(shift), .clk(clk), .sin(inp), .q1(out_10), .q2(out_11), .q3(out_12),
    .q4(out_13));  // open: d4, d3, d2, d1
  FullAdder fulladder_1 (.A(dflipflop_1_q), .B(out_9), .Cin(out_13), .Sum(fulladder_1_sum), .Count(fulladder_1_count));
  DFlipFlop dflipflop_1 (.D(fulladder_1_count), .Rst(reset), .Clk(clk), .Q(dflipflop_1_q));  // open: NotQ
endmodule

module DFlipFlop (
  input  D,
  input  Rst,
  input  Clk,
  output Q,
  output NotQ
);

  wire and_1_out, dlatch_1_q, not_1_out, not_2_out;

  Clock sysclk ();  // open: out
  not not_1 (not_1_out, Rst);
  not not_2 (not_2_out, Clk);
  and and_1 (and_1_out, D, not_1_out);
  DLatch dlatch_1 (.D(and_1_out), .Clk(not_2_out), .Q(dlatch_1_q));  // open: NotQ
  DLatch dlatch_2 (.D(dlatch_1_q), .Clk(not_2_out), .Q(Q), .NotQ(NotQ));
endmodule

module DLatch (
  input  D,
  input  Clk,
  output Q,
  output NotQ
);

  wire nand_1_out, nand_2_out, not_1_out;

  Clock sysclk ();  // open: out
  not not_1 (not_1_out, D);
  nand nand_1 (nand_1_out, D, Clk);
  nand nand_2 (nand_2_out, Clk, not_1_out);
  nand nand_3 (Q, nand_1_out, NotQ);
  nand nand_4 (NotQ, Q, nand_2_out);
endmodule

module JKFlipFlop (
  input  Init,
  input  J,
  input  K,
  input  Rst,
  output Q,
  output NotQ
);

  wire and_1_out, and_2_out, and_3_out, Clk_out, not_1_out, not_2_out, or_1_out, or_2_out, or_3_out,
       srlatch_1_notq, srlatch_1_q;

  Clock #(.highDuration(2), .lowDuration(2)) Clk (.out(Clk_out));
  Clock sysclk ();  // open: out
  not not_1 (not_1_out, Rst);
  and and_1 (and_1_out, J, not_1_out);
  or or_1 (or_1_out, K, Rst);
  and and_2 (and_2_out, NotQ, and_1_out);
  and and_3 (and_3_out, or_1_out, Q);
  or or_2 (or_2_out, Rst, Clk_out);
  not not_2 (not_2_out, Clk_out);
  SRLatch srlatch_1 (.S(and_2_out), .Clk(or_2_out), .R(and_3_out), .Q(srlatch_1_q), .NotQ(srlatch_1_notq));
  or or_3 (or_3_out, Rst, not_2_out);
  SRLatch srlatch_2 (.S(srlatch_1_q), .Clk(or_3_out), .R(srlatch_1_notq), .Q(Q), .NotQ(NotQ));
endmodule

module SRLatch (
  input  S,
  input  Clk,
  input  R,
  output Q,
  output NotQ
);

  wire nand_1_out, nand_2_out;

  Clock sysclk ();  // open: out
  nand nand_1 (nand_1_out, S, Clk);
  nand nand_2 (nand_2_out, Clk, R);
  nand nand_3 (Q, nand_1_out, NotQ);
  nand nand_4 (NotQ, Q, nand_2_out);
endmodule

module SequenceDetector (
  input  [1:0] X,
  output Q1Out,
  output Z,
  output Q2Out
);

  wire and_1_out, and_2_out, and_3_out, and_4_out, Clk_out, not_1_out, not_2_out;

  not not_1 (not_1_out, X[1]);
  Clock #(.highDuration(2), .lowDuration(2)) Clk (.out(Clk_out));
  Clock sysclk ();  // open: out
  not not_2 (not_2_out, X[0]);
  and and_1 (and_1_out, X[0], not_1_out, Q2Out);
  and and_2 (and_2_out, not_2_out, not_1_out);
  DFlipFlop q1 (.D(and_1_out), .Clk(Clk_out), .Q(Q1Out));  // open: Rst, NotQ
  DFlipFlop q0 (.D(and_2_out), .Clk(Clk_out), .Q(Q2Out));  // open: Rst, NotQ
  and and_3 (and_3_out, Q1Out, X[1], X[0]);
  and and_4 (and_4_out, Q2Out, X[1], X[0]);
  or or_1 (Z, and_3_out, and_4_out);
endmodule

module SequenceDetectorMoore (
  input  [1:0] X,
  output Q1Out,
  output Z,
  output Q0Out
);

  wire and_1_out, and_2_out, and_3_out, and_4_out, and_5_out, Clk_out, not_1_out, not_2_out, or_1_out,
       or_2_out, Q0_notq, Q1_notq;

  Clock sysclk ();  // open: out
  and and_1 (and_1_out, Q1_notq, Q0Out);
  and and_2 (and_2_out, Q1Out, Q0_notq, X[0], X[1]);
  not not_1 (not_1_out, X[0]);
  not not_2 (not_2_out, X[1]);
  and and_3 (and_3_out, and_1_out, X[0]);
  and and_4 (and_4_out, not_1_out, not_2_out);
  or or_1 (or_1_out, and_3_out, and_2_out);
  and and_5 (and_5_out, and_3_out, X[1]);
  or or_2 (or_2_out, and_2_out, and_5_out, and_4_out);
  Clock #(.highDuration(2), .lowDuration(2)) Clk (.out(Clk_out));
  DFlipFlop Q1 (.D(or_1_out), .Clk(Clk_out), .Q(Q1Out), .NotQ(Q1_notq));  // open: Rst
  DFlipFlop Q0 (.D(or_2_out), .Clk(Clk_out), .Q(Q0Out), .NotQ(Q0_notq));  // open: Rst
  and and_6 (Z, Q1Out, Q0Out);
endmodule

module OneBitShiftRegister (
  input  D,
  input  Rst,
  input  Clk,
  output Q,
  output NotQ
);

  wire not_1_out;

  not not_1 (not_1_out, Clk);
  DFlipFlop dflipflop_1 (.D(D), .Rst(Rst), .Clk(not_1_out), .Q(Q), .NotQ(NotQ));
endmodule

module FourBitShiftRegister (
  input  D,
  input  Rst,
  input  Clk,
  output out_4
);

  wire not_1_out, onebitshiftregister_1_q, onebitshiftregister_2_q, onebitshiftregister_3_q;

  not not_1 (not_1_out, Clk);
  OneBitShiftRegister onebitshiftregister_1 (
    .D(D), .Rst(Rst), .Clk(not_1_out), .Q(onebitshiftregister_1_q));  // open: NotQ
  OneBitShiftRegister onebitshiftregister_2 (
    .D(onebitshiftregister_1_q), .Rst(Rst), .Clk(not_1_out), .Q(onebitshiftregister_2_q));  // open: NotQ
  OneBitShiftRegister onebitshiftregister_3 (
    .D(onebitshiftregister_2_q), .Rst(Rst), .Clk(not_1_out), .Q(onebitshiftregister_3_q));  // open: NotQ
  OneBitShiftRegister onebitshiftregister_4 (
    .D(onebitshiftregister_3_q), .Rst(Rst), .Clk(not_1_out), .Q(out_4));  // open: NotQ
endmodule

module SerialAdder (
  input  Serial_Input,
  input  Reset,
  input  Clock,
  output Sum,
  output Carry
);

  wire dflipflop_1_q, fulladder_1_count, fulladder_1_sum;

  FourBitShiftRegister fourbitshiftregister_1 (.D(fulladder_1_sum), .Rst(Reset), .Clk(Clock), .out_4(Sum));
  FourBitShiftRegister fourbitshiftregister_2 (.D(Serial_Input), .Rst(Reset), .Clk(Clock), .out_4(Carry));
  DFlipFlop dflipflop_1 (.D(fulladder_1_count), .Rst(Reset), .Clk(Clock), .Q(dflipflop_1_q));  // open: NotQ
  FullAdder fulladder_1 (.A(dflipflop_1_q), .B(Sum), .Cin(Carry), .Sum(fulladder_1_sum), .Count(fulladder_1_count));
endmodule

module chronoSerialAdder (
  output out_1,
  output out_2,
  output out_3,
  output out_4,
  output out_5,
  output out_6,
  output out_7,
  output out_8
);

  wire clk_out, inp_out, load_out, reset_out, shift_out;

  Clock #(.highDuration(4), .lowDuration(4), .phaseOffset(4)) load (.out(load_out));
  Clock #(.highDuration(8), .lowDuration(8), .phaseOffset(8)) shift (.out(shift_out));
  Clock clk (.out(clk_out));
  Clock #(.highDuration(2), .lowDuration(2), .phaseOffset(2)) inp (.out(inp_out));
  Clock #(.lowDuration(50)) reset (.out(reset_out));
  SerialAdderv2 serialadderv2_1 (
    .load(load_out), .shift(shift_out), .clk(clk_out), .inp(inp_out), .reset(reset_out), .out_6(out_1),
    .out_7(out_2), .out_8(out_3), .out_9(out_4), .out_10(out_5), .out_11(out_6), .out_12(out_7),
    .out_13(out_8));
endmodule

module chronoshiftregister (
  output out_1,
  output out_2,
  output out_3,
  output out_4
);

  wire clk_out, d1_out, d2_out, d3_out, d4_out, load_out, reset_out, shift_out, sin_out;

  Clock #(.lowDuration(200)) reset (.out(reset_out));
  Clock #(.highDuration(64), .lowDuration(64)) load (.out(load_out));
  Clock #(.highDuration(128), .lowDuration(128)) shift (.out(shift_out));
  Clock clk (.out(clk_out));
  Clock #(.highDuration(2), .lowDuration(2)) d4 (.out(d4_out));
  Clock #(.highDuration(4), .lowDuration(4)) d3 (.out(d3_out));
  Clock #(.highDuration(8), .lowDuration(8)) d2 (.out(d2_out));
  Clock #(.highDuration(16), .lowDuration(16)) d1 (.out(d1_out));
  Clock #(.highDuration(32), .lowDuration(32)) sin (.out(sin_out));
  FourBitShiftRegisterv2 fourbitshiftregisterv2_1 (
    .reset(reset_out), .load(load_out), .shift(shift_out), .clk(clk_out), .d4(d4_out), .d3(d3_out),
    .d2(d2_out), .d1(d1_out), .sin(sin_out), .q1(out_1), .q2(out_2), .q3(out_3), .q4(out_4));
endmodule
